# Fritzing sketch trtr01 (saved by Fritzing 0.9.4)
perfboards: 1

parts:
  Q3_P75NF75_L = Basic FET N-Channel [package="TO220 [THT]"]
  Q4_P75NF75_R = Basic FET N-Channel [package="TO220 [THT]"]
  U1_817C_R = Sharp PC817 [package=THT]
  U2_817C_L = Sharp PC817 [package=THT]
  R4 = Resistor [tolerance=±5% resistance=47 package=THT]
  R2 = Resistor [tolerance=±5% resistance=47 package=THT]
  R1 = Resistor [tolerance=±5% resistance=470 package=THT]
  R3 = Resistor [tolerance=±5% resistance=470 package=THT]
  R5 = Resistor [tolerance=±5% resistance=1k package=THT]
  R6 = Resistor [tolerance=±5% resistance=1k package=THT]
  M_L+out = female pin header, 1 pin [form="♀ (female)"]
  M_R+out = female pin header, 1 pin [form="♀ (female)"]
  M_L-out = female pin header, 1 pin [form="♀ (female)"]
  M_R-out = female pin header, 1 pin [form="♀ (female)"]
  Relay_+ = female pin header, 1 pin [form="♀ (female)"]
  Relay_- = female pin header, 1 pin [form="♀ (female)"]
  R7 = Resistor [tolerance=±5% resistance=4.7k package=THT]
  ACCEL_400-4300Ohm = Screw terminal - 2 pins [package=THT]
  A2 = female pin header, 1 pin [form="♀ (female)"]
  GND = female pin header, 1 pin [form="♀ (female)"]
  5V_IN = female pin header, 1 pin [form="♀ (female)"]
  D3_REV = female pin header, 1 pin [form="♀ (female)"]
  D2 = Rectifier Diode [part_number=1N4001 package="300 mil [THT]"]
  D1 = Rectifier Diode [part_number=1N4001 package="300 mil [THT]"]
  Q5_K4272 = Basic FET N-Channel [package="D2Pak [SMD]"]
  R8 = Resistor [tolerance=±5% resistance=47 package=THT]
  D3 = Rectifier Diode [part_number=1N4001 package="300 mil [THT]"]
  R9 = Resistor [tolerance=±5% resistance=10k package=THT]
  D4_Schottky = Rectifier Diode [part_number=1N4001 package="300 mil [THT]"]
  PWM_9_L = female pin header, 1 pin [form="♀ (female)"]
  PWM_10_R = female pin header, 1 pin [form="♀ (female)"]
  D4 = Rectifier Diode [part_number=1N4001 package="300 mil [THT]"]
  D5 = Rectifier Diode [part_number=1N4001 package="300 mil [THT]"]

nets:
  N1: Q3_P75NF75_L.gate, U2_817C_L.Pin_3, R5.Pin_0
  N2: Q3_P75NF75_L.drain, M_L-out.pin1, D2.anode, D5.anode
  GND: Q3_P75NF75_L.source, Q4_P75NF75_R.source, U1_817C_R.Pin_2, U2_817C_L.Pin_2, R5.Pin_1, R6.Pin_1, R7.Pin_1, GND.pin1, Q5_K4272.source, R9.Pin_1
  N3: Q4_P75NF75_R.gate, U1_817C_R.Pin_3, R6.Pin_0
  N4: Q4_P75NF75_R.drain, M_R-out.pin1, D1.anode, D4.anode
  N5: U1_817C_R.Pin_1, R1.Pin_1
  N6: U1_817C_R.Pin_4, R4.Pin_1
  N7: U2_817C_L.Pin_1, R3.Pin_1
  N8: U2_817C_L.Pin_4, R2.Pin_1
  12V: R4.Pin_0, R2.Pin_0, M_L+out.pin1, M_R+out.pin1, Relay_+.pin1, D2.cathode, D1.cathode, D3.cathode, D4_Schottky.cathode, D4.cathode, D5.cathode
  N9: R1.Pin_0, PWM_10_R.pin1
  N10: R3.Pin_0, PWM_9_L.pin1
  N11: Relay_-.pin1, Q5_K4272.drain, D3.anode, D4_Schottky.anode
  N12: R7.Pin_0, ACCEL_400-4300Ohm.pin1, A2.pin1
  N13: ACCEL_400-4300Ohm.pin2, 5V_IN.pin1
  N14: D3_REV.pin1, R8.Pin_0
  N15: Q5_K4272.Gate, R8.Pin_1, R9.Pin_0
